# Fritzing sketch LDR_alarm_system_with_sound (saved by Fritzing 0.9.3b)
breadboards: 1

parts:
  Part1 = Arduino Uno (Rev3)
  LED1 = LED - 5mm [color="Green (560nm)" package="5 mm [THT]"]
  R1 = Resistor [tolerance=±5% resistance=10k package=THT]
  LED2 = LED - 5mm [color="Red (635nm)" package="5 mm [THT]"]
  R2 = Resistor [tolerance=±5% resistance=10k package=THT]
  J1 = Piezo Speaker
  J2 = Screw terminal - 2 pins [package=THT]
  S1 = Pushbutton [package="[THT]"]
  R3 = Resistor [tolerance=±5% resistance=10k package=THT]
  R4 = Photocell (LDR) [package=THT]
  R5 = Resistor [tolerance=±5% resistance=10k package=THT]

nets:
  N1: Part1.D9_PWM, J1.pin2, J2.pin1
  N2: Part1.D10_PWM/SS, R2.Pin_0
  N3: Part1.D11_PWM/MOSI, R1.Pin_0
  N4: Part1.D3_PWM, R4.pin_0, R5.Pin_1
  N5: Part1.D6_PWM, S1.Pin_3, S1.Pin_4, R3.Pin_1
  N6: Part1.5V, S1.Pin_1, S1.Pin_2, R5.Pin_0
  N7: Part1.GND, LED1.cathode, LED2.cathode, J1.pin1, J2.pin2, R3.Pin_0, R4.pin_1
  N8: LED1.anode, R1.Pin_1
  N9: LED2.anode, R2.Pin_1
